# Fritzing sketch Strawberry (saved by Fritzing 1.0.3b)
circuit board: 8.46667cm x 5.64444cm

parts:
  Part1 = Adafruit Feather 32u4 Bluefruit [part_number="Adafruit #2829"]
  BATT2 = 4xAA Switchable Battery Pack w/Bare Wire
  Part2 = Adafruit TB6612 DC and Stepper Motor Driver [part_number="Adafruit #2448"]
  Part3 = Adafruit TB6612 DC and Stepper Motor Driver [part_number="Adafruit #2448"]
  J1 = Basic Servo  # not connected
  Grove1 = Grove OLED 128x96
  U1 = LIPO-110mAh [package=lipo-110]  # not connected
  M1 = DC Motor [voltage_(max)=6V voltage_(min)=3V]  # not connected
  M2 = DC Motor [voltage_(max)=6V voltage_(min)=3V]  # not connected

nets:
  N1: Part1.A5, Part2.AIN1
  N2: Part1.A4, Part2.AIN2
  N3: Part1.A3, Part3.BIN2
  N4: Part1.A2, Part3.BIN1
  N5: Part1.A1, Part3.AIN1
  N6: Part1.A0, Part3.AIN2
  GND: Part1.GND, BATT2.NEG, Part2.GND, Part3.GND, Grove1.GND
  VCC: Part1.+3V3, Part2.VCC, Part2.STBY, Part3.VCC, Part3.STBY, Grove1.VCC
  N7: Part1.13, Part3.PWMA
  N8: Part1.11, Part3.PWMB
  N9: Part1.10, Part2.PWMA
  N10: Part1.3, Grove1.SCL
  N11: Part1.2, Grove1.SDA
  N12: BATT2.POS, Part3.PWRIN

custom parts:
  Adafruit Feather 32u4 Bluefruit: This is the Adafruit Feather 32u4 Bluefruit - our take on an 'all-in-one' Arduino-compatible + Bluetooth Low Energy with built in USB and battery charging. Its an Adafruit Feather 32u4 with a BTLE module, ready to rock! We have other boards in the Feather family, check'em out here. Bluetooth Low Energy is the hottest new low-power, 2.4GHz spectrum wireless protocol. In particular, its the only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
  4xAA Switchable Battery Pack w/Bare Wire: 4xAA Switchable Battery Pack with Bare Wire connection
  Adafruit TB6612 DC and Stepper Motor Driver: Spin two DC motors, step one bi-polar or uni-polar stepper, or fire off two solenoids with 1.2A per channel using the TB6612. These are perhaps better known as "the drivers in our assembled Adafruit Motorshield or Motor HAT." We really like these dual H-bridges, so if you want to control motors without a shield or HAT these are easy to include on any solderless breadboard or perma-proto.
