# Fritzing sketch Strawberry_layout (saved by Fritzing 1.0.3b)
circuit board: 8.46667cm x 5.64444cm
perfboards: 2

parts:
  Part1 = Adafruit Feather 32u4 Bluefruit [part_number="Adafruit #2829"]
  Part2 = Adafruit TB6612 DC and Stepper Motor Driver [part_number="Adafruit #2448"]
  Part3 = Adafruit TB6612 DC and Stepper Motor Driver [part_number="Adafruit #2448"]
  Grove1 = Grove OLED 128x96
  U1 = LIPO-110mAh [package=lipo-110]  # not connected
  M1 = DC Motor [voltage_(max)=6V voltage_(min)=3V]
  M2 = DC Motor [voltage_(max)=6V voltage_(min)=3V]
  J2 = double row female pin header, 24 pins [form="♀ (female)"]
  J3 = double row female pin header, 24 pins [form="♀ (female)"]
  BATT2 = 4xAA Switchable Battery Pack w/Bare Wire
  J4 = Basic Servo
  J5 = double row female pin header, 24 pins [form="♀ (female)"]
  J6 = double row female pin header, 24 pins [form="♀ (female)"]

nets:
  N1: Part1.A5, J5.pin23
  N2: Part1.A4, J5.pin22
  N3: Part1.A3, J5.pin10
  N4: Part1.A2, J5.pin9
  N5: Part1.A1, J5.pin7
  N6: Part1.A0, J5.pin6
  GND: Part1.GND, Grove1.GND, J5.pin4, J6.pin24
  +3V3: Part1.+3V3, Grove1.VCC, J5.pin3, J6.pin23
  N7: Part1.13, J5.pin5
  N8: Part1.11, J5.pin11
  N9: Part1.10, J5.pin24
  N10: Part1.3, Grove1.SCL, J6.pin21
  N11: Part1.2, Grove1.SDA, J6.pin22
  N12: Part2.PWRIN, Part3.GND, J3.pin21
  N13: Part2.GND, J2.pin17
  N14: Part2.STBY, Part3.VCC, J3.pin22
  N15: Part2.AIN1, J3.pin3
  N16: Part2.AIN2, J3.pin2
  N17: Part2.PWMA, J3.pin1
  N18: Part2.MOTORA1, J2.pin19
  N19: Part2.MOTORA2, J2.pin18
  N20: Part3.Vmotor, Part3.PWRIN, BATT2.POS
  N21: Part3.PWMB, J3.pin20
  N22: Part3.BIN2, J3.pin19
  N23: Part3.BIN1, J3.pin18
  N24: Part3.AIN1, J3.pin16
  N25: Part3.AIN2, J3.pin15
  N26: Part3.PWMA, J3.pin14
  N27: Part3.MOTORA1, J2.pin12
  N28: Part3.MOTORA2, J2.pin11
  N29: Part3.MOTORB2, J2.pin5
  N30: Part3.MOTORB1, J2.pin4
  N31: M1.pin_1, J6.pin10
  N32: M1.pin_2, J6.pin11
  N33: M2.pin_1, J6.pin4
  N34: M2.pin_2, J6.pin5
  N35: J4.gnd, J6.pin17
  N36: J4.vcc, J6.pin18
  N37: J4.pulse, J6.pin19

notes:
  PWMA - 11
  AIN2 - A3
  AIN1 - A2
  STBY - Vcc
  BIN1 - A1
  BIN2 - A0
  PWMB - 13
  GND - GND
  Vcc - Vcc
  PWMA - 10
  AIN2 - A5
  AIN1 - A4
  STBY - Vcc
  BIN1
  BIN2
  PWMB
  GND
  Vcc

custom parts:
  Adafruit Feather 32u4 Bluefruit: This is the Adafruit Feather 32u4 Bluefruit - our take on an 'all-in-one' Arduino-compatible + Bluetooth Low Energy with built in USB and battery charging. Its an Adafruit Feather 32u4 with a BTLE module, ready to rock! We have other boards in the Feather family, check'em out here. Bluetooth Low Energy is the hottest new low-power, 2.4GHz spectrum wireless protocol. In particular, its the only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
  Adafruit TB6612 DC and Stepper Motor Driver: Spin two DC motors, step one bi-polar or uni-polar stepper, or fire off two solenoids with 1.2A per channel using the TB6612. These are perhaps better known as "the drivers in our assembled Adafruit Motorshield or Motor HAT." We really like these dual H-bridges, so if you want to control motors without a shield or HAT these are easy to include on any solderless breadboard or perma-proto.
  4xAA Switchable Battery Pack w/Bare Wire: 4xAA Switchable Battery Pack with Bare Wire connection
